# Fritzing sketch arduivis_model5_multipleinputs (saved by Fritzing 0.8.7b)
breadboards: 1

parts:
  Part1 = Arduino Uno (Rev3)
  LED1 = LED - 5mm [color="Red (633nm)" package="5 mm [THT]"]
  LED2 = LED - 5mm [color="Red (633nm)" package="5 mm [THT]"]
  LED3 = LED - 5mm [color="Red (633nm)" package="5 mm [THT]"]
  LED4 = LED - 5mm [color="Red (633nm)" package="5 mm [THT]"]

nets:
  N1: Part1.D9_PWM, LED4.anode
  N2: Part1.GND, LED1.cathode, LED2.cathode, LED3.cathode, LED4.cathode
  N3: Part1.D3_PWM, LED1.anode
  N4: Part1.D5_PWM, LED2.anode
  N5: Part1.D6_PWM, LED3.anode
