# Fritzing sketch MOSFET-Magnet (saved by Fritzing 0.9.3b)
breadboards: 1

parts:
  Q1 = Basic FET N-Channel [package="TO220 [THT]"]
  Part1 = Arduino Uno (Rev3) - ICSP
  R1 = Resistor [tolerance=±5% resistance=220 package=THT]
  J2 = Power Jack [package=power_jack_smd]

nets:
  N1: Q1.gate, R1.Pin_0
  GND: Q1.source, Part1.GND, J2.GND
  N2: Part1.D13/SCK, R1.Pin_1

// code stored in the sketch: MOSFET-LED.ino
void setup() {
  Serial.begin(9600);
  pinMode(13, OUTPUT);
}

void loop() {
  int j = Serial.parseInt();
  if (j == 1) {
    digitalWrite(13, HIGH);
  } else if (j == 0) {
    digitalWrite(13, LOW);
  }
}
